# Fritzing sketch kazkar_wiring_diagram (saved by Fritzing 0.9.9b)
breadboards: 1

parts:
  Part1 = Arduino Uno (Rev3) - ICSP
  microSD1 = MicroSD Card Module
  S1 = Pushbutton [package="[THT]"]
  S2 = Pushbutton [package="[THT]"]
  S3 = Pushbutton [package="[THT]"]
  SP1 = SPEAKER [package=pcb_mount_speaker]

nets:
  N1: Part1.D9_PWM, SP1.-
  N2: Part1.D11_PWM/MOSI, microSD1.MOSI
  N3: Part1.D12/MISO, microSD1.MISO
  N4: Part1.D13/SCK, microSD1.SCK
  N5: Part1.D4, microSD1.CS
  N6: Part1.D5_PWM, S2.Pin_1, S2.Pin_2
  N7: Part1.D6_PWM, S3.Pin_1, S3.Pin_2
  N8: Part1.D7, S1.Pin_1, S1.Pin_2
  5V: Part1.5V, microSD1.VCC
  GND: Part1.GND, microSD1.GND, S1.Pin_3, S1.Pin_4, S2.Pin_3, S2.Pin_4, S3.Pin_3, S3.Pin_4, SP1.+

notes:
  microSD:
  CS -> D4
  SCK -> D13
  MOSI -> D11
  MISO -> D12
  VCC -> 5V or 3.3V*
  GND -> GND
  *Use 5V only if your breakout/module has onboard regulation / level shifting.
  If it is a bare socket or simple 3.3V breakout, use 3.3V.
  *Use 5V only if your breakout/module has onboard regulation / level shifting.
  If it is a bare socket or simple 3.3V breakout, use 3.3V.
